# Fritzing sketch wiring (saved by Fritzing 0.9.0b)

parts:
  Teensy_3_1 = Teensy 3.1
  - = molex pin header, 5 pins [form=molex]
  + = molex pin header, 5 pins [form=molex]
  S = molex pin header, 5 pins [form=molex]

nets:
  N1: Teensy_3_1.GND, -.pin1
  N2: Teensy_3_1.D1, S.pin1
  N3: Teensy_3_1.D2, S.pin2
  N4: Teensy_3_1.D3, S.pin3
  N5: Teensy_3_1.D4, S.pin4
  N6: Teensy_3_1.D5, S.pin5
  N7: Teensy_3_1.VUSB, +.pin1
